# Fritzing sketch RPI Dutzo Controller (saved by Fritzing 0.9.8b)

parts:
  Raspberry_Pi_1 = Raspberry Pi 3 [part_number=RPI-3-V1.2]
  DHT1 = DHT22 Humidity and Temperature Sensor
  R1 = Resistor [tolerance=±5% power=0.25 resistance=10k package=THT]
  JP1 = Header 3 [package=molex-1x3_lock]
  Dutzo_Controller_FAN_/_aRGB = Neopixel Strip -- White (30/m)

nets:
  3V3: Raspberry_Pi_1.3v3, DHT1.VDD, R1.Pin_0
  N1: Raspberry_Pi_1.GIPO4, DHT1.NULL, R1.Pin_1
  GND: Raspberry_Pi_1.GND, DHT1.GND, JP1.1, Dutzo_Controller_FAN_/_aRGB.GND
  N2: Raspberry_Pi_1.GIPO18, JP1.2, Dutzo_Controller_FAN_/_aRGB.Din

custom parts:
  Neopixel Strip -- White (30/m): These NeoPixel strips have 30 digitally-addressable pixel LEDs per meter and are very affordable and are only 12.5 mm wide, 10 mm if you remove the strip from the casing.
